// Digital circuit cpu.dig as structural Verilog
module cpu (
  input  clk,
  output [31:0] OUT1,
  output [31:0] OUT2,
  output [31:0] RegINBus,
  output [1:0] out_5,
  output [31:0] RegOUTBus,
  output [31:0] MemoryAddressBus
);

  wire comparator_1_eq, comparator_2_eq, comparator_3_eq, comparator_4_eq, comparator_5_eq, decoder_1_out_1,
       decoder_1_out_2, decoder_1_out_3, decoder_1_out_4, decoder_1_out_5, decoder_1_out_6, decoder_1_out_7,
       decoder_1_out_8, decoder_1_out_9, decoder_1_out_10, decoder_1_out_11, decoder_1_out_12,
       decoder_1_out_13, decoder_1_out_14, decoder_1_out_15, decoder_2_out_0, decoder_2_out_1,
       decoder_2_out_2, decoder_2_out_3, decoder_2_out_4, decoder_2_out_5, decoder_2_out_6, decoder_2_out_7,
       decoder_2_out_8, decoder_2_out_9, decoder_2_out_10, decoder_2_out_11, decoder_2_out_12,
       decoder_2_out_13, decoder_2_out_14, decoder_2_out_15, decoder_3_out_0, decoder_3_out_1,
       decoder_3_out_2, decoder_3_out_3, decoder_3_out_4, decoder_3_out_5, decoder_3_out_6, decoder_3_out_7,
       decoder_3_out_8, decoder_3_out_9, decoder_3_out_10, decoder_3_out_11, decoder_3_out_12,
       decoder_3_out_13, decoder_3_out_14, decoder_3_out_15, demultiplexer_7_out_0, demultiplexer_7_out_1,
       IRSwitcher_out, not_1_out, not_2_out, or_1_out, or_2_out, or_3_out, or_5_out, pulldown_1_out,
       pulldown_17_out, pulldown_18_out, pullup_1_out;
  wire [2:0] demultiplexer_8_out_0, multiplexer_3_out_3;
  wire [4:0] demultiplexer_4_out_0, demultiplexer_5_out_1, demultiplexer_6_out_0, demultiplexer_9_out_0,
       multiplexer_3_out_2, multiplexer_3_out_4;
  wire [5:5] comparator_6_eq;
  wire [6:0] demultiplexer_1_out_0, demultiplexer_2_out_1, demultiplexer_3_out_0;
  wire [11:0] demultiplexer_5_out_0, demultiplexer_9_out_1;
  wire [19:0] demultiplexer_8_out_1;
  wire [31:0] add_1_s, and_1_out, barrelshifter_1_out, bitextender_1_out, bitextender_2_out,
       bitextender_3_out, counterpreset_1_out, d_ff_1_q, d_ff_2_q, d_ff_3_q, d_ff_4_q, d_ff_5_q, d_ff_6_q,
       d_ff_7_q, d_ff_8_q, d_ff_9_q, d_ff_10_q, d_ff_11_q, d_ff_12_q, d_ff_13_q, d_ff_14_q, d_ff_15_q,
       d_ff_16_q, d_ff_17_q, multiplexer_1_out, multiplexer_2_out, multiplexer_4_out, multiplexer_5_out,
       multiplexer_6_out, multiplexer_7_out, multiplexer_8_out, multiplexer_9_out, multiplexer_10_out,
       multiplexer_11_out, multiplexer_12_out, multiplexer_13_out, multiplexer_14_out, multiplexer_15_out,
       multiplexer_16_out, multiplexer_17_out, multiplexer_18_out, multiplexer_19_out, multiplexer_20_out,
       multiplexer_21_out, multiplexer_22_out, multiplexer_23_out, multiplexer_24_out, not_3_out, not_4_out,
       not_5_out, or_4_out, pulldown_2_out, pulldown_21_out, rom_1_d, xor_1_out;
  wire [31:2] multiplexer_3_out;

  or or_1 (or_1_out, comparator_5_eq, comparator_1_eq);
  Comparator #(.Bits(4)) comparator_1 (.a(multiplexer_3_out[5:2]), .b(4'b1100), .eq(comparator_1_eq));  // open: gt, lt
  Demultiplexer #(.Bits(7)) demultiplexer_1 (
    .sel(or_2_out), .in(multiplexer_3_out[31:25]), .out_0(demultiplexer_1_out_0),
    .out_1(demultiplexer_8_out_1[19:13]));
  Demultiplexer #(.Bits(7)) demultiplexer_2 (
    .sel(or_1_out), .in(demultiplexer_1_out_0), .out_0(demultiplexer_5_out_0[11:5]),
    .out_1(demultiplexer_2_out_1));
  Demultiplexer #(.Bits(7)) demultiplexer_3 (
    .sel(comparator_5_eq), .in(demultiplexer_2_out_1), .out_0(demultiplexer_3_out_0),
    .out_1(demultiplexer_9_out_1[11:5]));
  Counter IRSwitcher (.en(rom_1_d[12]), .C(not_1_out), .clr(pulldown_1_out), .out(IRSwitcher_out));  // open: ovf
  PullDown pulldown_1 (.out(pulldown_1_out));
  Demultiplexer #(.Bits(5)) demultiplexer_4 (
    .sel(or_2_out), .in(multiplexer_3_out[24:20]), .out_0(demultiplexer_4_out_0),
    .out_1(demultiplexer_8_out_1[12:8]));
  Demultiplexer #(.Bits(5)) demultiplexer_5 (
    .sel(or_1_out), .in(demultiplexer_4_out_0), .out_0(demultiplexer_5_out_0[4:0]),
    .out_1(demultiplexer_5_out_1));
  Demultiplexer #(.Bits(5)) demultiplexer_6 (
    .sel(or_2_out), .in(multiplexer_3_out_4), .out_0(demultiplexer_6_out_0),
    .out_1(demultiplexer_8_out_1[7:3]));
  Multiplexer #(.Bits(32)) multiplexer_1 (
    .sel(demultiplexer_7_out_0), .in_0(d_ff_1_q), .in_1(multiplexer_4_out), .out(multiplexer_1_out));
  Demultiplexer demultiplexer_7 (
    .sel(IRSwitcher_out), .in(rom_1_d[13]), .out_0(demultiplexer_7_out_0), .out_1(demultiplexer_7_out_1));
  Demultiplexer #(.Bits(3)) demultiplexer_8 (
    .sel(or_2_out), .in(multiplexer_3_out_3), .out_0(demultiplexer_8_out_0),
    .out_1(demultiplexer_8_out_1[2:0]));
  D_FF #(.Bits(32)) d_ff_1 (.D(multiplexer_1_out), .C(not_1_out), .Q(d_ff_1_q));  // open: nQ
  or or_2 (or_2_out, comparator_4_eq, or_3_out);
  or or_3 (or_3_out, comparator_3_eq, comparator_2_eq);
  BitExtender #(.inputBits(20), .outputBits(32)) bitextender_1 (.in(demultiplexer_8_out_1), .out(bitextender_1_out));
  BitExtender #(.inputBits(12), .outputBits(32)) bitextender_2 (.in(demultiplexer_5_out_0), .out(bitextender_2_out));
  Comparator #(.Bits(4)) comparator_2 (.a(multiplexer_3_out[5:2]), .b(4'b1101), .eq(comparator_2_eq));  // open: gt, lt
  Comparator #(.Bits(4)) comparator_3 (.a(multiplexer_3_out[5:2]), .b(4'b0101), .eq(comparator_3_eq));  // open: gt, lt
  Comparator #(.Bits(4)) comparator_4 (.a(multiplexer_3_out[5:2]), .b(4'b1011), .eq(comparator_4_eq));  // open: gt, lt
  Multiplexer #(.Bits(32)) multiplexer_2 (
    .sel(demultiplexer_7_out_1), .in_0(d_ff_2_q), .in_1(multiplexer_4_out), .out(multiplexer_2_out));
  assign or_4_out = bitextender_3_out | bitextender_1_out | bitextender_2_out;  // Or or_4, 32 bits wide
  assign RegOUTBus = rom_1_d[10] ? or_4_out : 32'bz;  // Driver driver_1
  D_FF #(.Bits(32)) d_ff_2 (.D(multiplexer_2_out), .C(not_1_out), .Q(d_ff_2_q));  // open: nQ
  Multiplexer #(.Bits(32)) multiplexer_3 (
    .sel(IRSwitcher_out), .in_0(d_ff_2_q), .in_1(d_ff_1_q),
    .out({multiplexer_3_out[31:20], multiplexer_3_out_4, multiplexer_3_out_3, multiplexer_3_out_2, multiplexer_3_out[6:2], out_5}));
  BitExtender #(.inputBits(12), .outputBits(32)) bitextender_3 (.in(demultiplexer_9_out_1), .out(bitextender_3_out));
  RAMDualPort #(.AddrBits(20), .Bits(32)) ramdualport_1 (
    .A(MemoryAddressBus[19:0]), .Din(RegOUTBus), .str(rom_1_d[15]), .C(clk), .ld(rom_1_d[14]), .D(RegINBus));
  PullDown #(.Bits(32)) pulldown_2 (.out(pulldown_2_out));
  Multiplexer #(.Bits(32)) multiplexer_4 (
    .sel(rom_1_d[11]), .in_0(RegINBus), .in_1(pulldown_2_out), .out(multiplexer_4_out));
  Demultiplexer #(.Bits(5)) demultiplexer_9 (
    .sel(comparator_5_eq), .in(multiplexer_3_out_2), .out_0(demultiplexer_9_out_0),
    .out_1(demultiplexer_9_out_1[4:0]));
  ROM #(.AddrBits(9), .Bits(32)) rom_1 (
    .A({demultiplexer_8_out_0, comparator_6_eq[5], multiplexer_3_out[6:2]}), .sel(1'b1), .D(rom_1_d));
  Comparator #(.Bits(4)) comparator_5 (.a(multiplexer_3_out[5:2]), .b(4'b1000), .eq(comparator_5_eq));  // open: gt, lt
  Comparator #(.Bits(7)) comparator_6 (
    .a(demultiplexer_3_out_0), .b(7'b0100000), .eq(comparator_6_eq[5]));  // open: gt, lt
  not not_1 (not_1_out, clk);
  PullDown pulldown_3 (.out(rom_1_d[14]));
  PullDown pulldown_4 (.out(rom_1_d[15]));
  PullDown pulldown_5 (.out(rom_1_d[12]));
  PullDown pulldown_6 (.out(rom_1_d[13]));
  PullDown pulldown_7 (.out(rom_1_d[10]));
  PullDown pulldown_8 (.out(rom_1_d[11]));
  Decoder #(.Selector_Bits(4)) decoder_1 (
    .sel(demultiplexer_9_out_0[3:0]), .out_1(decoder_1_out_1), .out_2(decoder_1_out_2),
    .out_3(decoder_1_out_3), .out_4(decoder_1_out_4), .out_5(decoder_1_out_5), .out_6(decoder_1_out_6),
    .out_7(decoder_1_out_7), .out_8(decoder_1_out_8), .out_9(decoder_1_out_9), .out_10(decoder_1_out_10),
    .out_11(decoder_1_out_11), .out_12(decoder_1_out_12), .out_13(decoder_1_out_13),
    .out_14(decoder_1_out_14), .out_15(decoder_1_out_15));  // open: out_0
  PullDown pulldown_9 (.out(rom_1_d[8]));
  PullDown pulldown_10 (.out(rom_1_d[9]));
  PullDown pulldown_11 (.out(rom_1_d[6]));
  PullDown pulldown_12 (.out(rom_1_d[7]));
  Multiplexer #(.Bits(32)) multiplexer_5 (
    .sel(not_2_out), .in_0(RegOUTBus), .in_1(counterpreset_1_out), .out(multiplexer_5_out));
  not not_2 (not_2_out, rom_1_d[0]);
  assign RegOUTBus = rom_1_d[9] ? OUT2 : 32'bz;  // Driver driver_2
  assign not_3_out = ~OUT1;  // Not not_3, 32 bits wide
  assign not_4_out = ~RegOUTBus;  // Not not_4, 32 bits wide
  PullDown pulldown_13 (.out(rom_1_d[4]));
  PullDown pulldown_14 (.out(rom_1_d[5]));
  or or_5 (or_5_out, not_2_out, rom_1_d[1]);
  Multiplexer #(.Bits(32)) multiplexer_6 (.sel(rom_1_d[3]), .in_0(OUT1), .in_1(not_3_out), .out(multiplexer_6_out));
  Multiplexer #(.Bits(32)) multiplexer_7 (
    .sel(rom_1_d[4]), .in_0(RegOUTBus), .in_1(not_4_out), .out(multiplexer_7_out));
  PullDown pulldown_15 (.out(rom_1_d[2]));
  PullDown pulldown_16 (.out(rom_1_d[3]));
  CounterPreset #(.Bits(32), .isProgramCounter("true")) counterpreset_1 (
    .en(pullup_1_out), .C(clk), .dir(pulldown_17_out), .in(multiplexer_5_out), .ld(or_5_out),
    .clr(pulldown_18_out), .out(counterpreset_1_out));  // open: ovf
  PullUp pullup_1 (.out(pullup_1_out));
  PullDown pulldown_17 (.out(pulldown_17_out));
  PullDown pulldown_18 (.out(pulldown_18_out));
  Add #(.Bits(32)) add_1 (.a(multiplexer_6_out), .b(multiplexer_7_out), .c_i(rom_1_d[4]), .s(add_1_s));  // open: c_o
  assign and_1_out = multiplexer_6_out & multiplexer_7_out;  // And and_1, 32 bits wide
  assign xor_1_out = multiplexer_6_out ^ multiplexer_7_out;  // XOr xor_1, 32 bits wide
  BarrelShifter #(.Bits(32)) barrelshifter_1 (
    .in(multiplexer_6_out), .shift(multiplexer_7_out[5:0]), .out(barrelshifter_1_out));
  PullDown pulldown_19 (.out(rom_1_d[1]));
  PullDown pulldown_20 (.out(rom_1_d[0]));
  assign MemoryAddressBus = rom_1_d[2] ? counterpreset_1_out : 32'bz;  // Driver driver_3
  Multiplexer #(.Bits(32)) multiplexer_8 (
    .sel(decoder_1_out_1), .in_0(d_ff_3_q), .in_1(RegINBus), .out(multiplexer_8_out));
  Multiplexer #(.Bits(32)) multiplexer_9 (
    .sel(decoder_1_out_2), .in_0(d_ff_4_q), .in_1(RegINBus), .out(multiplexer_9_out));
  Multiplexer #(.Bits(32)) multiplexer_10 (
    .sel(decoder_1_out_3), .in_0(d_ff_5_q), .in_1(RegINBus), .out(multiplexer_10_out));
  Multiplexer #(.Bits(32)) multiplexer_11 (
    .sel(decoder_1_out_4), .in_0(d_ff_6_q), .in_1(RegINBus), .out(multiplexer_11_out));
  Multiplexer #(.Bits(32)) multiplexer_12 (
    .sel(decoder_1_out_5), .in_0(d_ff_7_q), .in_1(RegINBus), .out(multiplexer_12_out));
  Multiplexer #(.Bits(32)) multiplexer_13 (
    .sel(decoder_1_out_6), .in_0(d_ff_8_q), .in_1(RegINBus), .out(multiplexer_13_out));
  Multiplexer #(.Bits(32)) multiplexer_14 (
    .sel(decoder_1_out_7), .in_0(d_ff_9_q), .in_1(RegINBus), .out(multiplexer_14_out));
  Multiplexer #(.Bits(32)) multiplexer_15 (
    .sel(decoder_1_out_8), .in_0(d_ff_10_q), .in_1(RegINBus), .out(multiplexer_15_out));
  Multiplexer #(.Bits(32)) multiplexer_16 (
    .sel(decoder_1_out_9), .in_0(d_ff_11_q), .in_1(RegINBus), .out(multiplexer_16_out));
  Multiplexer #(.Bits(32)) multiplexer_17 (
    .sel(decoder_1_out_10), .in_0(d_ff_12_q), .in_1(RegINBus), .out(multiplexer_17_out));
  Multiplexer #(.Bits(32)) multiplexer_18 (
    .sel(decoder_1_out_11), .in_0(d_ff_13_q), .in_1(RegINBus), .out(multiplexer_18_out));
  Multiplexer #(.Bits(32)) multiplexer_19 (
    .sel(decoder_1_out_12), .in_0(d_ff_14_q), .in_1(RegINBus), .out(multiplexer_19_out));
  Multiplexer #(.Bits(32)) multiplexer_20 (
    .sel(decoder_1_out_13), .in_0(d_ff_15_q), .in_1(RegINBus), .out(multiplexer_20_out));
  Multiplexer #(.Bits(32)) multiplexer_21 (
    .sel(decoder_1_out_14), .in_0(d_ff_16_q), .in_1(RegINBus), .out(multiplexer_21_out));
  Multiplexer #(.Bits(32)) multiplexer_22 (
    .sel(decoder_1_out_15), .in_0(d_ff_17_q), .in_1(RegINBus), .out(multiplexer_22_out));
  PullDown #(.Bits(32)) pulldown_21 (.out(pulldown_21_out));
  D_FF #(.Bits(32)) d_ff_3 (.D(multiplexer_8_out), .C(clk), .Q(d_ff_3_q));  // open: nQ
  D_FF #(.Bits(32)) d_ff_4 (.D(multiplexer_9_out), .C(clk), .Q(d_ff_4_q));  // open: nQ
  D_FF #(.Bits(32)) d_ff_5 (.D(multiplexer_10_out), .C(clk), .Q(d_ff_5_q));  // open: nQ
  D_FF #(.Bits(32)) d_ff_6 (.D(multiplexer_11_out), .C(clk), .Q(d_ff_6_q));  // open: nQ
  D_FF #(.Bits(32)) d_ff_7 (.D(multiplexer_12_out), .C(clk), .Q(d_ff_7_q));  // open: nQ
  D_FF #(.Bits(32)) d_ff_8 (.D(multiplexer_13_out), .C(clk), .Q(d_ff_8_q));  // open: nQ
  D_FF #(.Bits(32)) d_ff_9 (.D(multiplexer_14_out), .C(clk), .Q(d_ff_9_q));  // open: nQ
  D_FF #(.Bits(32)) d_ff_10 (.D(multiplexer_15_out), .C(clk), .Q(d_ff_10_q));  // open: nQ
  D_FF #(.Bits(32)) d_ff_11 (.D(multiplexer_16_out), .C(clk), .Q(d_ff_11_q));  // open: nQ
  D_FF #(.Bits(32)) d_ff_12 (.D(multiplexer_17_out), .C(clk), .Q(d_ff_12_q));  // open: nQ
  D_FF #(.Bits(32)) d_ff_13 (.D(multiplexer_18_out), .C(clk), .Q(d_ff_13_q));  // open: nQ
  D_FF #(.Bits(32)) d_ff_14 (.D(multiplexer_19_out), .C(clk), .Q(d_ff_14_q));  // open: nQ
  D_FF #(.Bits(32)) d_ff_15 (.D(multiplexer_20_out), .C(clk), .Q(d_ff_15_q));  // open: nQ
  D_FF #(.Bits(32)) d_ff_16 (.D(multiplexer_21_out), .C(clk), .Q(d_ff_16_q));  // open: nQ
  D_FF #(.Bits(32)) d_ff_17 (.D(multiplexer_22_out), .C(clk), .Q(d_ff_17_q));  // open: nQ
  Multiplexer #(.Selector_Bits(2), .Bits(32)) multiplexer_23 (
    .sel({rom_1_d[5], rom_1_d[6]}), .in_0(add_1_s), .in_1(and_1_out), .in_2(xor_1_out),
    .in_3(barrelshifter_1_out), .out(multiplexer_23_out));
  assign OUT1 = decoder_2_out_0 ? pulldown_21_out : 32'bz;  // Driver driver_4
  assign OUT2 = decoder_3_out_0 ? pulldown_21_out : 32'bz;  // Driver driver_5
  assign OUT1 = decoder_2_out_1 ? d_ff_3_q : 32'bz;  // Driver driver_6
  assign OUT2 = decoder_3_out_1 ? d_ff_3_q : 32'bz;  // Driver driver_7
  assign OUT1 = decoder_2_out_2 ? d_ff_4_q : 32'bz;  // Driver driver_8
  assign OUT2 = decoder_3_out_2 ? d_ff_4_q : 32'bz;  // Driver driver_9
  assign OUT1 = decoder_2_out_3 ? d_ff_5_q : 32'bz;  // Driver driver_10
  assign OUT2 = decoder_3_out_3 ? d_ff_5_q : 32'bz;  // Driver driver_11
  assign OUT1 = decoder_2_out_4 ? d_ff_6_q : 32'bz;  // Driver driver_12
  assign OUT2 = decoder_3_out_4 ? d_ff_6_q : 32'bz;  // Driver driver_13
  assign OUT1 = decoder_2_out_5 ? d_ff_7_q : 32'bz;  // Driver driver_14
  assign OUT2 = decoder_3_out_5 ? d_ff_7_q : 32'bz;  // Driver driver_15
  assign OUT1 = decoder_2_out_6 ? d_ff_8_q : 32'bz;  // Driver driver_16
  assign OUT2 = decoder_3_out_6 ? d_ff_8_q : 32'bz;  // Driver driver_17
  assign OUT1 = decoder_2_out_7 ? d_ff_9_q : 32'bz;  // Driver driver_18
  assign OUT2 = decoder_3_out_7 ? d_ff_9_q : 32'bz;  // Driver driver_19
  assign OUT1 = decoder_2_out_8 ? d_ff_10_q : 32'bz;  // Driver driver_20
  assign OUT2 = decoder_3_out_8 ? d_ff_10_q : 32'bz;  // Driver driver_21
  assign OUT1 = decoder_2_out_9 ? d_ff_11_q : 32'bz;  // Driver driver_22
  assign OUT2 = decoder_3_out_9 ? d_ff_11_q : 32'bz;  // Driver driver_23
  assign OUT1 = decoder_2_out_10 ? d_ff_12_q : 32'bz;  // Driver driver_24
  assign OUT2 = decoder_3_out_10 ? d_ff_12_q : 32'bz;  // Driver driver_25
  assign OUT1 = decoder_2_out_11 ? d_ff_13_q : 32'bz;  // Driver driver_26
  assign OUT2 = decoder_3_out_11 ? d_ff_13_q : 32'bz;  // Driver driver_27
  assign OUT1 = decoder_2_out_12 ? d_ff_14_q : 32'bz;  // Driver driver_28
  assign OUT2 = decoder_3_out_12 ? d_ff_14_q : 32'bz;  // Driver driver_29
  assign OUT1 = decoder_2_out_13 ? d_ff_15_q : 32'bz;  // Driver driver_30
  assign OUT2 = decoder_3_out_13 ? d_ff_15_q : 32'bz;  // Driver driver_31
  assign OUT1 = decoder_2_out_14 ? d_ff_16_q : 32'bz;  // Driver driver_32
  assign OUT2 = decoder_3_out_14 ? d_ff_16_q : 32'bz;  // Driver driver_33
  assign OUT1 = decoder_2_out_15 ? d_ff_17_q : 32'bz;  // Driver driver_34
  assign OUT2 = decoder_3_out_15 ? d_ff_17_q : 32'bz;  // Driver driver_35
  assign not_5_out = ~multiplexer_23_out;  // Not not_5, 32 bits wide
  Multiplexer #(.Bits(32)) multiplexer_24 (
    .sel(rom_1_d[7]), .in_0(multiplexer_23_out), .in_1(not_5_out), .out(multiplexer_24_out));
  assign RegINBus = rom_1_d[8] ? multiplexer_24_out : 32'bz;  // Driver driver_36
  Decoder #(.Selector_Bits(4)) decoder_2 (
    .sel(demultiplexer_6_out_0[3:0]), .out_0(decoder_2_out_0), .out_1(decoder_2_out_1),
    .out_2(decoder_2_out_2), .out_3(decoder_2_out_3), .out_4(decoder_2_out_4), .out_5(decoder_2_out_5),
    .out_6(decoder_2_out_6), .out_7(decoder_2_out_7), .out_8(decoder_2_out_8), .out_9(decoder_2_out_9),
    .out_10(decoder_2_out_10), .out_11(decoder_2_out_11), .out_12(decoder_2_out_12),
    .out_13(decoder_2_out_13), .out_14(decoder_2_out_14), .out_15(decoder_2_out_15));
  Decoder #(.Selector_Bits(4)) decoder_3 (
    .sel(demultiplexer_5_out_1[3:0]), .out_0(decoder_3_out_0), .out_1(decoder_3_out_1),
    .out_2(decoder_3_out_2), .out_3(decoder_3_out_3), .out_4(decoder_3_out_4), .out_5(decoder_3_out_5),
    .out_6(decoder_3_out_6), .out_7(decoder_3_out_7), .out_8(decoder_3_out_8), .out_9(decoder_3_out_9),
    .out_10(decoder_3_out_10), .out_11(decoder_3_out_11), .out_12(decoder_3_out_12),
    .out_13(decoder_3_out_13), .out_14(decoder_3_out_14), .out_15(decoder_3_out_15));

  // Notes on the sheet:
  //   R type
  //   ~I_type
  //   This is here because 
  //   only the last
  //   field differs in 
  //   R/S/B types.
  //   I type
  //   J type
  //   U type
  //   IR2
  //   RD(5)
  //   RS1(5)
  //   RS2(5)
  //   IR1
  //   IMM(32)
  //   funct7
  //   funct3
  //   Control dignals change on the
  //   down-clock to ensure that
  //   everything finishes
  //   updating, since everything else
  //   work on the up-clock.
  //   High bit
  //   Low nibble
  //   contents of rom_1 (hex, n*v repeats v):
  //   7005,7005,7005,7005,3d04,7005,7005,7005,7005,7005,7005,7005,7005,7005,7005,7005,7005,
  //   7005,7005,7005,7005,7005,7005,7005,7005,7005,7005,7005,7005,7005,7005,7005,7005,7005,
  //   7005,7005,3d04,7005,7005,7005,7005,7005,7005,7005,7005,7005,7005,7005,7005,7005,7005,
  //   7005,7005,7005,7005,7005,7005,7005,7005,7005,7005,7005,7005,7005,7005,7005,7005,7005,
  //   7005,7005,7005,7005,7005,7005,7005,7005,7005,7005,7005,7005,7005,7005,7005,7005,7005,
  //   7005,7005,7005,7005,7005,7005,7005,7005,7005,7005,7005,7005,7005,7005,7005,7005,7005,
  //   7005,7005,7005,7005,7005,7005,7005,7005,7005,7005,7005,7005,7005,7005,7005,7005,7005,
  //   7005,7005,7005,7005,7005,7005,7005,7005,7005,7005,7005,7005,7005,7005,7005,7005,7005,
  //   7005,7005,7005,7005,7005,7005,7005,7005,7005,7005,7005,7005,7005,7005,7005,7005,7005,
  //   7005,7005,7005,7005,7005,7005,7005,7005,7005,7005,7005,7005,7005,7005,7005,7005,7005,
  //   7005,7005,7005,7005,7005,7005,7005,7005,7005,7005,7005,7005,7005,7005,7005,7005,7005,
  //   7005,7005,7005,7005,7005,7005,7005,7005,7005,7005,7005,7005,7005,7005,7005,7005,7005,
  //   7005,7005,7005,7005,7005,7005,7005,7005,7005,7005,7005,7005,7005,7005,7005,7005,7005,
  //   7005,7005,7005,7005,7005,7005,7005,7005,7005,7005,7005,7005,7005,7005,7005,7005,7005,
  //   7005,7005,7005,7005,7005,7005,7005,7005,7005,7005,7005,7005,7005,7005,7005,7005,7005,
  //   7005,7005,7005,7005,7005,7005,7005,7005,7005,7005,7005,7005,7005,7005,7005,7005,7005,
  //   7005,7005,7005,7005,7005,7005,7005,7005,7005,7005,7005,7005,7005,7005,7005,7005,7005,
  //   7005,7005,7005,7005,7005,7005,7005,7005,7005,7005,7005,7005,7005,7005,7005,7005,7005,
  //   7005,7005,7005,7005,7005,7005,7005,7005,7005,7005,7005,7005,7005,7005,7005,7005,7005,
  //   7005,7005,7005,7005,7005,7005,7005,7005,7005,7005,7005,7005,7005,7005,7005,7005,7005,
  //   7005,7005,7005,7005,7005,7005,7005,7005,7005,7005,7005,7005,7005,7005,7005,7005,7005,
  //   7005,7005,7005,7005,7005,7005,7005,7005,7005,7005,7005,7005,7005,7005,7005,7005,7005,
  //   7005,7005,7005,7005,7005,7005,7005,7005,7005,7005,7005,7005,7005,7005,7005,7005,7005,
  //   7005,7005,7005,7005,7005,7005,7005,7005,7005,7005,7005,7005,7005,7005,7005,7005,7005,
  //   7005,7005,7005,7005,7005,7005,7005,7005,7005,7005,7005,7005,7005,7005,7005,7005,7005,
  //   7005,7005,7005,7005,7005,7005,7005,7005,7005,7005,7005,7005,7005,7005,7005,7005,7005,
  //   7005,7005,7005,7005,7005,7005,7005,7005,7005,7005,7005,7005,7005,7005,7005,7005,7005,
  //   7005,7005,7005,7005,7005,7005,7005,7005,7005,7005,7005,7005,7005,7005,7005,7005,7005,
  //   7005,7005,7005,7005,7005,7005,7005,7005,7005,7005,7005,7005,7005,7005,7005,7005,7005,
  //   7005,7005,7005,7005,7005,7005,7005,7005,7005,7005,7005,7005,7005,7005,7005,7005,7005,
  //   7005,7005
  //   ID
  //   S/B type
  //   RAM_ENO
  //   RAM_LOAD
  //   IR_SWITCH_EN
  //   IR_LOAD
  //   CNTRL_IMM_OUT
  //   IR_ZR
  //   REG_OUT
  //   ALU_OUT
  //   ALU_INVOUT
  //   ALU_OP 0
  //   Enables input, but also enables counting,
  //   but if load is on it will latch the value
  //   instead of counting
  //   CI
  //   ALU_INVB
  //   ALU_OP 1
  //   RS1
  //   ALU_INVA
  //   PC_OUT
  //   PC_LOAD
  //   PC_ENIN/_ENC
  //   CLK
  //   SEL2
endmodule
